// Logisim project TWO BIT HALF ADDER.circ as structural Verilog: 1 circuit, main circuit main
module main (
  input  a,
  input  b,
  output SUM,
  output CARRY
);

  xor x_or (SUM, a, b);
  and AND (CARRY, b, a);
endmodule
